# Fritzing sketch touch_bb_1 (saved by Fritzing 0.9.3b)
breadboards: 1

parts:
  VCC1 = 4 x AAA Battery Mount
  LED1 = smd LED [color="Red (633nm)" package="1206 [SMD]"]
  R2 = Resistor [tolerance=±5% resistance=1k package="2512 [SMD]"]
  R3 = Resistor [tolerance=±5% resistance=1k package="2512 [SMD]"]
  R4 = Resistor [tolerance=±5% resistance=1k package="2512 [SMD]"]
  R5 = Resistor [tolerance=±5% resistance=1k package="2512 [SMD]"]

nets:
  N1: VCC1.-, LED1.cathode
  N2: VCC1.+, R2.Pin_1, R3.Pin_1, R4.Pin_1, R5.Pin_1
  N3: LED1.anode, R2.Pin_0, R3.Pin_0, R4.Pin_0, R5.Pin_0
