# Fritzing sketch touch_bb_2 (saved by Fritzing 0.9.3b)
breadboards: 1

parts:
  5V = 4 x AAA Battery Mount
  LED1 = smd LED [color="Red (633nm)" package="1206 [SMD]"]
  R3 = Resistor [tolerance=±5% resistance=1k package="2512 [SMD]"]
  R1 = Resistor [tolerance=±5% resistance=1k package="2512 [SMD]"]
  R2 = Resistor [tolerance=±5% resistance=1k package="2512 [SMD]"]

nets:
  N1: 5V.-, LED1.cathode
  N2: 5V.+, R1.Pin_1, R2.Pin_1
  N3: LED1.anode, R3.Pin_0
  N4: R3.Pin_1, R1.Pin_0, R2.Pin_0
